// Logisim project AlarmCounter.circ as structural Verilog: 1 circuit, main circuit main
module main (
);

  wire and_1_out, clock_1_out, j_k_ff_1_q, j_k_ff_1_qn, multiplexer_1_out, multiplexer_2_out, nand_1_out,
       not_1_out, xor_1_out, xor_2_out;
  wire [1:0] counter_1_q;
  wire [3:0] bcd_to_7_segment_decoder_1_p1;
  wire [4:0] BTNC_out, register_1_q;
  wire [6:0] counter_2_q, multiplexer_3_out, register_2_q, register_3_q, register_4_q, register_5_q;

  Button BTNC (.out(BTNC_out[0]));
  Button BTNL (.out(BTNC_out[1]));
  Button BTNR (.out(BTNC_out[2]));
  Button BTNU (.out(BTNC_out[3]));
  Button BTND (.out(BTNC_out[4]));
  Clock clock_1 (.out(clock_1_out));
  Register #(.width(5)) register_1 (.D(BTNC_out), .en(1'b1), .clk(clock_1_out), .Q(register_1_q));  // open: clr
  xor xor_1 (xor_1_out, register_1_q[1], register_1_q[2]);
  not not_1 (not_1_out, register_1_q[1]);
  Counter #(.max('h3), .width(2)) counter_1 (
    .up(multiplexer_1_out), .count(xor_1_out), .clk(clock_1_out), .Q(counter_1_q));  // open: clr, load, D, carry
  Multiplexer multiplexer_1 (.in0(1'b0), .in1(1'b1), .out(multiplexer_1_out), .sel(not_1_out));
  xor xor_2 (xor_2_out, register_1_q[4], register_1_q[3]);
  Multiplexer multiplexer_2 (.in0(1'b1), .in1(1'b0), .out(multiplexer_2_out), .sel(register_1_q[4]));
  nand nand_1 (nand_1_out, counter_1_q[1], counter_1_q[0]);
  Register #(.width(7)) register_2 (
    .D(counter_2_q), .en(nand_1_out), .clk(clock_1_out), .Q(register_2_q));  // open: clr
  J_K_Flip_Flop j_k_ff_1 (
    .J(counter_1_q[0]), .K(counter_1_q[1]), .Q(j_k_ff_1_q), .Qn(j_k_ff_1_qn));  // open: clk, preset, reset
  Register #(.width(7)) register_3 (
    .D(counter_2_q), .en(j_k_ff_1_q), .clk(clock_1_out), .Q(register_3_q));  // open: clr
  Multiplexer #(.select(2), .width(7)) multiplexer_3 (
    .in0(register_2_q), .in1(register_3_q), .in2(register_4_q), .in3(register_5_q), .out(multiplexer_3_out),
    .sel(counter_1_q));
  Register #(.width(7)) register_4 (
    .D(counter_2_q), .en(j_k_ff_1_qn), .clk(clock_1_out), .Q(register_4_q));  // open: clr
  Counter #(.max('h7f), .width(7)) counter_2 (
    .load(xor_1_out), .up(multiplexer_2_out), .count(xor_2_out), .clk(clock_1_out), .D(multiplexer_3_out),
    .Q(counter_2_q));  // open: clr, carry
  Register #(.width(7)) register_5 (.D(counter_2_q), .en(and_1_out), .clk(clock_1_out), .Q(register_5_q));  // open: clr
  and and_1 (and_1_out, counter_1_q[1], counter_1_q[0]);
  _7_Segment_Display u_7_segment_display_1 ();  // open: g, f, a, b, e, d, c, dp
  // BCD_to_7_Segment_decoder bcd_to_7_segment_decoder_1: pin names not known; wires that end beside it: bcd_to_7_segment_decoder_1_p1
  assign bcd_to_7_segment_decoder_1_p1 = {{1{1'b0}}, register_2_q[6:4]};  // Bit_Extender bit_extender_1
  _7_Segment_Display u_7_segment_display_2 ();  // open: g, f, a, b, e, d, c, dp
  // BCD_to_7_Segment_decoder bcd_to_7_segment_decoder_2: pin names not known; wires that end beside it: register_2_q[3:0]

  // Notes on the sheet:
  //   TimeMin
  //   TimeHour
  //   There maybe a problem in the enabling of the JK Flip Flop
  //   The counter save its count so when we move to another register and try to count it gives it that value
  //   AlarmMin
  //   AlarmHours
endmodule
