// Logisim project CUDP - Copy.circ as structural Verilog: 1 circuit, main circuit main
module main (
  input  [1:0] in_1,
  input  [3:0] in_2,
  input  [2:0] in_3,
  input  [3:0] in_4,
  input  [3:0] in_5,
  input  [2:0] in_6,
  input  [3:0] in_7,
  input  [2:0] in_8,
  input  [2:0] in_9,
  input  [6:0] in_10,
  input  [6:0] in_11,
  input  [4:0] in_12,
  input  [4:0] ConstantOne,
  input  [4:0] ConstantZero,
  input  [4:0] in_15,
  input  in_16
);

  wire AlarmSound_q, and_1_out, and_2_out, and_3_out, and_4_out, and_5_out, and_6_out, and_7_out, and_8_out,
       and_9_out, and_10_out, and_11_out, and_12_out, and_13_out, and_14_out, and_15_out, and_16_out,
       and_17_out, and_18_out, and_19_out, and_20_out, button_1_out, clock_1_out, d_ff_1_q, d_ff_2_q,
       decoder_1_out0, decoder_1_out1, decoder_1_out2, decoder_1_out3, multiplexer_11_out,
       multiplexer_12_out, nor_1_out, not_1_out, not_2_out, not_3_out, not_4_out, or_1_out, or_2_out,
       or_3_out, or_4_out, or_5_out, or_6_out, or_7_out, or_8_out, t_ff_1_q, ZFlag_out;
  wire [0:0] BL_q;
  wire [1:0] BL_Load_out, counter_5_q;
  wire [2:0] counter_1_q, counter_4_q, CurrentTimeHourTen_q, CurrentTimeMin_q_2, multiplexer_6_out,
       multiplexer_9_out;
  wire [3:0] bcd_to_7_segment_decoder_1_p1, bcd_to_7_segment_decoder_2_p1, bcd_to_7_segment_decoder_3_p1,
       bcd_to_7_segment_decoder_4_p1, bcd_to_7_segment_decoder_5_p1, bcd_to_7_segment_decoder_6_p1,
       bcd_to_7_segment_decoder_7_p1, counter_2_q, counter_3_q, CurrentTimeHour_q, CurrentTimeMin_q,
       multiplexer_1_out, multiplexer_2_out, multiplexer_8_out;
  wire [4:0] buttonState_q, LEDstate_q, multiplexer_10_out, subtractor_2_out, subtractor_3_out, undriven;
  wire [6:0] CurrentTimeMinOne_q;
  wire [13:0] SetAlarmMin_q, subtractor_1_out;
  wire [13:11] CurrentTimeHour_q_2;

  Clock clock_1 (.out(clock_1_out));
  Counter #(.max('h7), .width(3)) counter_1 (
    .load(and_1_out), .count(and_4_out), .clk(clock_1_out), .D(in_3), .Q(counter_1_q));  // open: clr, up, carry
  Counter #(.max('hf), .width(4)) counter_2 (
    .load(and_4_out), .count(1'b1), .clk(clock_1_out), .D(in_2), .Q(counter_2_q));  // open: clr, up, carry
  Counter #(.max('hf), .width(4)) counter_3 (
    .load(and_2_out), .count(1'b1), .clk(t_ff_1_q), .D(in_7), .Q(counter_3_q));  // open: clr, up, carry
  Counter #(.max('h7), .width(3)) counter_4 (
    .load(and_3_out), .count(and_2_out), .clk(t_ff_1_q), .D(in_9), .Q(counter_4_q));  // open: clr, up, carry
  and and_1 (and_1_out, counter_1_q[0], counter_1_q[1]);
  and and_2 (and_2_out, counter_3_q[3], counter_3_q[0]);
  and and_3 (and_3_out, counter_4_q[2], counter_4_q[1], and_2_out);
  Counter #(.max('h3), .width(2)) counter_5 (
    .load(and_6_out), .count(1'b1), .clk(clock_1_out), .D(in_1), .Q(counter_5_q));  // open: clr, up, carry
  and and_4 (and_4_out, counter_2_q[0], counter_2_q[1], counter_2_q[2], counter_2_q[3]);
  or Load_Zer0 (BL_Load_out[1], and_10_out, and_5_out);
  Button button_1 (.out(button_1_out));
  and and_5 (and_5_out, and_7_out, ~d_ff_1_q);  // AND_Gate
  Multiplexer #(.width(4)) multiplexer_1 (.in0(in_5), .in1(CurrentTimeMin_q), .out(multiplexer_1_out), .sel(1'b0));
  and and_6 (and_6_out, counter_5_q[1], counter_5_q[0]);
  and and_7 (and_7_out, and_8_out, not_1_out);
  Decoder #(.enable("false"), .select(2)) decoder_1 (
    .out0(decoder_1_out0), .out1(decoder_1_out1), .out2(decoder_1_out2), .out3(decoder_1_out3),
    .sel(counter_5_q));
  T_Flip_Flop t_ff_1 (.T(and_1_out), .clk(clock_1_out), .Q(t_ff_1_q));  // open: Qn, reset, preset
  not not_1 (not_1_out, ZFlag_out);
  or or_1 (or_1_out, BL_Load_out[1], button_1_out);
  not not_2 (not_2_out, not_4_out);
  and and_8 (and_8_out, d_ff_2_q, not_2_out);
  D_Flip_Flop d_ff_1 (.D(or_2_out), .clk(clock_1_out), .Q(d_ff_1_q));  // open: Qn, preset, reset
  or or_2 (or_2_out, and_9_out, and_13_out);
  Multiplexer #(.select(2), .width(4)) multiplexer_2 (
    .in0(CurrentTimeMinOne_q[3:0]), .in1(bcd_to_7_segment_decoder_6_p1), .in2(bcd_to_7_segment_decoder_4_p1),
    .in3(bcd_to_7_segment_decoder_2_p1), .out(multiplexer_2_out), .sel(counter_5_q));
  or or_3 (or_3_out, and_17_out, and_12_out);
  Counter #(.max('hf), .width(4)) CurrentTimeMinOne (
    .load(or_3_out), .count(and_3_out), .clk(t_ff_1_q), .D(multiplexer_1_out), .Q(CurrentTimeMinOne_q[3:0]));  // open: clr, up, carry
  D_Flip_Flop d_ff_2 (.D(or_1_out), .clk(clock_1_out), .Q(d_ff_2_q));  // open: Qn, preset, reset
  and and_9 (and_9_out, ZFlag_out, and_8_out);
  not not_3 (not_3_out, nor_1_out);
  and and_10 (and_10_out, d_ff_1_q, not_3_out);
  and and_11 (and_11_out, not_4_out, d_ff_2_q);
  _7_Segment_Display u_7_segment_display_1 ();  // open: g, f, a, b, e, d, c, dp
  // BCD_to_7_Segment_decoder bcd_to_7_segment_decoder_1: pin names not known; wires that end beside it: bcd_to_7_segment_decoder_1_p1
  Multiplexer #(.width(4)) multiplexer_3 (
    .in1(multiplexer_2_out), .out(bcd_to_7_segment_decoder_1_p1), .sel(decoder_1_out3));  // open: in0
  _7_Segment_Display u_7_segment_display_2 ();  // open: g, f, a, b, e, d, c, dp
  // BCD_to_7_Segment_decoder bcd_to_7_segment_decoder_2: pin names not known; wires that end beside it: bcd_to_7_segment_decoder_2_p1
  and and_12 (and_12_out, CurrentTimeMinOne_q[3], and_3_out, CurrentTimeMinOne_q[0]);
  and and_13 (and_13_out, nor_1_out, d_ff_1_q);
  assign bcd_to_7_segment_decoder_2_p1 = {{1{1'b0}}, CurrentTimeHourTen_q};  // Bit_Extender bit_extender_1
  _7_Segment_Display u_7_segment_display_3 ();  // open: g, f, a, b, e, d, c, dp
  // BCD_to_7_Segment_decoder bcd_to_7_segment_decoder_3: pin names not known; wires that end beside it: bcd_to_7_segment_decoder_3_p1
  Multiplexer #(.width(4)) multiplexer_4 (
    .in1(multiplexer_2_out), .out(bcd_to_7_segment_decoder_3_p1), .sel(decoder_1_out2));  // open: in0
  _7_Segment_Display u_7_segment_display_4 (.dp(t_ff_1_q));  // open: g, f, a, b, e, d, c
  // BCD_to_7_Segment_decoder bcd_to_7_segment_decoder_4: pin names not known; wires that end beside it: bcd_to_7_segment_decoder_4_p1
  or or_4 (or_4_out, and_17_out, and_14_out);
  _7_Segment_Display u_7_segment_display_5 ();  // open: g, f, a, b, e, d, c, dp
  // BCD_to_7_Segment_decoder bcd_to_7_segment_decoder_5: pin names not known; wires that end beside it: bcd_to_7_segment_decoder_5_p1
  Multiplexer #(.width(4)) multiplexer_5 (
    .in1(multiplexer_2_out), .out(bcd_to_7_segment_decoder_5_p1), .sel(decoder_1_out1));  // open: in0
  _7_Segment_Display u_7_segment_display_6 ();  // open: g, f, a, b, e, d, c, dp
  // BCD_to_7_Segment_decoder bcd_to_7_segment_decoder_6: pin names not known; wires that end beside it: bcd_to_7_segment_decoder_6_p1
  assign bcd_to_7_segment_decoder_6_p1 = {{1{1'b0}}, CurrentTimeMinOne_q[6:4]};  // Bit_Extender bit_extender_2
  Counter #(.max('h7), .width(3)) CurrentTimeMinTen (
    .load(or_4_out), .count(and_12_out), .clk(t_ff_1_q), .D(multiplexer_6_out), .Q(CurrentTimeMinOne_q[6:4]));  // open: clr, up, carry
  Multiplexer #(.width(3)) multiplexer_6 (.in0(in_6), .in1(CurrentTimeMin_q_2), .out(multiplexer_6_out), .sel(1'b0));
  // Probe on and_11_out
  _7_Segment_Display u_7_segment_display_7 ();  // open: g, f, a, b, e, d, c, dp
  // BCD_to_7_Segment_decoder bcd_to_7_segment_decoder_7: pin names not known; wires that end beside it: bcd_to_7_segment_decoder_7_p1
  Multiplexer #(.width(4)) multiplexer_7 (
    .in1(multiplexer_2_out), .out(bcd_to_7_segment_decoder_7_p1), .sel(decoder_1_out0));  // open: in0
  _7_Segment_Display u_7_segment_display_8 ();  // open: g, f, a, b, e, d, c, dp
  // BCD_to_7_Segment_decoder bcd_to_7_segment_decoder_8: pin names not known; wires that end beside it: CurrentTimeMinOne_q[3:0]
  and and_14 (and_14_out, CurrentTimeMinOne_q[6], and_12_out, CurrentTimeMinOne_q[4]);
  or or_5 (or_5_out, and_17_out, and_15_out);
  Multiplexer #(.width(4)) multiplexer_8 (.in0(in_4), .in1(CurrentTimeHour_q), .out(multiplexer_8_out), .sel(1'b0));
  Register #(.width(7)) CurrentTimeMin (
    .D(CurrentTimeMinOne_q), .clk(clock_1_out), .Q({CurrentTimeMin_q_2, CurrentTimeMin_q}));  // open: en, clr
  Counter #(.max('hf), .width(4)) CurrentTimeHourOne (
    .load(or_5_out), .count(and_14_out), .clk(t_ff_1_q), .D(multiplexer_8_out),
    .Q(bcd_to_7_segment_decoder_4_p1));  // open: clr, up, carry
  or BL_Load (BL_Load_out[0], and_9_out, and_13_out);
  or or_6 (or_6_out, and_17_out, and_18_out);
  and and_15 (and_15_out, bcd_to_7_segment_decoder_4_p1[3], bcd_to_7_segment_decoder_4_p1[0], and_14_out);
  Register #(.width(7)) CurrentTimeHour (
    .D({CurrentTimeHourTen_q, bcd_to_7_segment_decoder_4_p1}), .clk(clock_1_out),
    .Q({CurrentTimeHour_q_2, CurrentTimeHour_q}));  // open: en, clr
  T_Flip_Flop BL (.T(1'b1), .clk(clock_1_out), .Q(BL_q[0]));  // open: Qn, reset, preset
  Counter #(.max('h7), .width(3)) CurrentTimeHourTen (
    .load(or_6_out), .count(and_15_out), .clk(t_ff_1_q), .D(multiplexer_9_out), .Q(CurrentTimeHourTen_q));  // open: clr, up, carry
  Subtractor #(.width(14)) subtractor_1 (
    .a({CurrentTimeHour_q_2, CurrentTimeHour_q, CurrentTimeMin_q_2, CurrentTimeMin_q}), .b(SetAlarmMin_q),
    .out(subtractor_1_out));  // open: bin, bout
  and and_16 (and_16_out, bcd_to_7_segment_decoder_4_p1[0], bcd_to_7_segment_decoder_4_p1[1]);
  Multiplexer #(.width(3)) multiplexer_9 (.in0(in_8), .in1(CurrentTimeHour_q_2), .out(multiplexer_9_out), .sel(1'b0));
  Register #(.width(7)) SetAlarmMin (.D(in_10), .clk(clock_1_out), .Q(SetAlarmMin_q[6:0]));  // open: en, clr
  Multiplexer #(.select(2), .width(5)) multiplexer_10 (
    .in0(LEDstate_q), .in1({4'b0000, BL_q[0]}), .in2(in_15), .in3(undriven), .out(multiplexer_10_out),
    .sel(BL_Load_out));
  Multiplexer #(.select(2)) multiplexer_11 (
    .in0(AlarmSound_q), .in1(1'b1), .in2(in_16), .out(multiplexer_11_out), .sel(BL_Load_out));  // open: in3
  and and_17 (and_17_out, CurrentTimeHourTen_q[1], and_19_out, and_20_out, and_16_out);
  and and_18 (and_18_out, CurrentTimeHourTen_q[1], and_15_out);
  or or_7 (or_7_out, BL_Load_out[0], BL_Load_out[1]);
  and and_19 (and_19_out, CurrentTimeMinOne_q[6], CurrentTimeMinOne_q[4]);
  Register #(.width(7)) SetAlarmHour (.D(in_11), .clk(clock_1_out), .Q(SetAlarmMin_q[13:7]));  // open: en, clr
  Register #(.width(5)) LEDstate (
    .D(multiplexer_10_out), .en(or_7_out), .clk(clock_1_out), .Q(LEDstate_q));  // open: clr
  and and_20 (and_20_out, CurrentTimeMinOne_q[0], CurrentTimeMinOne_q[3]);
  nor ZFlag (ZFlag_out, subtractor_1_out[13], subtractor_1_out[12], subtractor_1_out[11], subtractor_1_out[10], subtractor_1_out[9], subtractor_1_out[8], subtractor_1_out[7], subtractor_1_out[6], subtractor_1_out[5], subtractor_1_out[4], subtractor_1_out[3], subtractor_1_out[2], subtractor_1_out[1], subtractor_1_out[0]);
  Register #(.width(5)) buttonState (.D(in_12), .clk(clock_1_out), .Q(buttonState_q));  // open: en, clr
  D_Flip_Flop AlarmSound (.D(multiplexer_12_out), .clk(clock_1_out), .Q(AlarmSound_q));  // open: Qn, preset, reset
  Multiplexer multiplexer_12 (.in0(AlarmSound_q), .in1(multiplexer_11_out), .out(multiplexer_12_out), .sel(or_7_out));
  Subtractor #(.width(5)) subtractor_2 (.a(buttonState_q), .b(ConstantOne), .out(subtractor_2_out));  // open: bin, bout
  Subtractor #(.width(5)) subtractor_3 (
    .a(buttonState_q), .b(ConstantZero), .out(subtractor_3_out));  // open: bin, bout
  LedBar #(.matrixcols(5)) ledbar_1 (
    .led0(LEDstate_q[4]), .led1(LEDstate_q[3]), .led2(LEDstate_q[2]), .led3(LEDstate_q[1]),
    .led4(LEDstate_q[0]));
  or or_8 (or_8_out, subtractor_2_out[0], subtractor_2_out[1], subtractor_2_out[2], subtractor_2_out[3], subtractor_2_out[4]);
  nor nor_1 (nor_1_out, subtractor_3_out[0], subtractor_3_out[1], subtractor_3_out[2], subtractor_3_out[3], subtractor_3_out[4]);
  not not_4 (not_4_out, or_8_out);

  // Notes on the sheet:
  //   ConstantOne: initial=0x1
  //   LEDstate <- 00000
  //   AlarmSound = 0
  //   Reset
  //   ZFlag == 1
  //   IF2
  //   LEDstate <-BL
  //   AlarmSound <- 1
  //   AlarmState
  //   Clock State
  //   buttonState == 00001
  //   IF1
  //   buttonState == 00000
  //   AlarmSound = 1
  //   LEDstate <- BL
  //   AL
  //   00 no load
  //   01 BL load
  //   10 ZeroLoad
  //   ZFlag Subtractor
  //   LEDstate MUX
  //   AlarmSound MUX
  //   buttonState != 00001
  //   buttonState == 0
  //   buttonState == 00001
endmodule
